# Fritzing sketch flow-project (saved by Fritzing 0.9.3b)
circuit board: 18.0305cm x 9.8563cm
breadboards: 1

parts:
  U1 = NodeMCU V3.0
  J1 = Screw terminal - 2 pins [package=THT]
  C1 = Capacitor Polarized [package=panasonic_g]
  Part1 = Arduino Mega ADK (Rev3)
  DO = screw terminal, 3 pins
  TUR = screw terminal, 3 pins
  PH = screw terminal, 3 pins
  ULTRA = screw terminal, 4 pins
  TEMP = screw terminal, 3 pins
  RELAY_4_CH = screw terminal, 7 pins
  SOLINOID = screw terminal, 3 pins
  STATUS = screw terminal, 3 pins
  LED1 = smd LED [color="Red (633nm)" package="0603 [SMD]"]
  R1 = Resistor [tolerance=±5% resistance=100 package="2010 [SMD]"]

nets:
  N1: U1.D0, Part1.D18/TX1
  N2: U1.D1, Part1.D10_PWM
  N3: U1.D2, Part1.D11_PWM
  N4: U1.D3, Part1.D19/RX1
  GND: U1.GND, J1.pin1, C1.+, Part1.GND, DO.pin1, TUR.pin1, PH.pin1, ULTRA.pin1, TEMP.pin1, RELAY_4_CH.pin1, RELAY_4_CH.pin6, SOLINOID.pin1, STATUS.pin1, LED1.cathode
  VIN: U1.Vin, J1.pin2, C1.-, Part1.VIN, DO.pin3, TUR.pin3, PH.pin3, ULTRA.pin4, TEMP.pin3, RELAY_4_CH.pin7, SOLINOID.pin3, STATUS.pin3, R1.Pin_1
  N5: Part1.A13, DO.pin2
  N6: Part1.A14, TUR.pin2
  N7: Part1.A15, PH.pin2
  N8: Part1.D23, STATUS.pin2
  N9: Part1.D25, SOLINOID.pin2
  N10: Part1.D31, RELAY_4_CH.pin2
  N11: Part1.D33, RELAY_4_CH.pin3
  N12: Part1.D35, RELAY_4_CH.pin4
  N13: Part1.D37, RELAY_4_CH.pin5
  N14: Part1.D49, TEMP.pin2
  N15: Part1.D51/MOSI, ULTRA.pin2
  N16: Part1.D53/SS, ULTRA.pin3
  N17: LED1.anode, R1.Pin_0

custom parts:
  NodeMCU V3.0: ESP8266 based NodeMCU
